// Logisim project tower.circ as structural Verilog: 12 circuits, main circuit Tower
module Tower (
);

  wire AI, ALUO, ARHI, ARHLO, ARHO, ARLI, ARLO, BI, BO, CLK, clock_1_out, DEC, F_CARRY, FI, FO, HI, HLI, HLO,
       HLT, HO, INCE, INCI, INCO, incrementer_1_incarry_out, INI, LI, LO, MI, MO, OPADD, OPNAND, OPNOT, OPSR,
       OPSUB, PCI, PCJ, PCO, RAMSTART, RESET, SPI, SPO, SPOA, SPSTART;
  wire [2:0] CONTROL_FLAGS;
  wire [3:0] alu_1_carry_out;
  wire [3:2] aluflags_1_data_out;
  wire [7:0] aluregisters_1_a_data_out, aluregisters_1_b_data_out, DATA_BUS, instructionregister_1_data_out;
  wire [15:0] ADDRESS_BUS;
  wire [39:0] controllogic_1_control_word;

  Clock clock_1 (.out(clock_1_out));
  and and_1 (CLK, clock_1_out, ~HLT);  // AND_Gate
  Button u_RESET (.out(RESET));
  // Probe on aluregisters_1_a_data_out
  ALURegisters aluregisters_1 (
    .CLK(CLK), .RESET(RESET), .A_DATA_IN(DATA_BUS), .AI(AI), .B_DATA_IN(DATA_BUS), .BI(BI),
    .A_DATA_OUT(aluregisters_1_a_data_out), .B_DATA_OUT(aluregisters_1_b_data_out));
  // Probe on aluregisters_1_b_data_out
  ProgramCounter programcounter_1 (
    .CLK(CLK), .RESET(RESET), .J(PCJ), .CO(PCO), .CE(PCI), .PC_ADDRESS_IN(ADDRESS_BUS),
    .PC_DATA_OUT(ADDRESS_BUS));
  MemoryRegisters memoryregisters_1 (
    .CLK(CLK), .RESET(RESET), .ADDRESS_IN(ADDRESS_BUS), .DATA_IN(DATA_BUS), .HI(HI), .LI(LI), .HO(HO),
    .LO(LO), .HLO(HLO), .HLI(HLI), .DATA_OUT(DATA_BUS), .ADDRESS_OUT(ADDRESS_BUS));
  InstructionRegister instructionregister_1 (
    .CLK(CLK), .RESET(RESET), .DATA_IN(DATA_BUS), .INI(INI), .DATA_OUT(instructionregister_1_data_out));
  ArgumentRegisters argumentregisters_1 (
    .CLK(CLK), .RESET(RESET), .DATA_IN(DATA_BUS), .HI(ARHI), .LI(ARLI), .HO(ARHO), .LO(ARLO), .HLO(ARHLO),
    .DATA_OUT(DATA_BUS), .ADDRESS_OUT(ADDRESS_BUS));
  assign DATA_BUS = BO ? aluregisters_1_b_data_out : 8'bz;  // Controlled_Buffer controlled_buffer_1
  // LedBar #(.inputtype("row")) ledbar_1: pin names not known; wires that end beside it: DATA_BUS
  // LedBar #(.inputtype("row"), .matrixcols(16)) ledbar_2: pin names not known; wires that end beside it: ADDRESS_BUS
  assign ADDRESS_BUS[8] = SPSTART ? SPSTART : 1'bz;  // Controlled_Buffer controlled_buffer_2
  assign ADDRESS_BUS[14] = RAMSTART ? RAMSTART : 1'bz;  // Controlled_Buffer controlled_buffer_3
  StackPointer stackpointer_1 (.CLK(CLK), .RESET(RESET), .DATA_IN(DATA_BUS), .SPI(SPI), .SPO(SPO), .DATA_OUT(DATA_BUS));
  Memory memory_1 (.CLK(CLK), .DATA_IN(DATA_BUS), .ADDR_IN(ADDRESS_BUS), .MI(MI), .MO(MO), .DATA_OUT(DATA_BUS));
  ControlLogic controllogic_1 (
    .CLK(CLK), .RESET(RESET), .INSTRUCTION(instructionregister_1_data_out), .FLAGS(CONTROL_FLAGS),
    .CONTROL_WORD({controllogic_1_control_word[39], SPSTART, RAMSTART, INI, MO, MI, FO, FI, INCO, INCI, DEC, INCE, OPSR, OPNAND, OPNOT, OPSUB, OPADD, ALUO, ARHLO, ARLO, ARLI, ARHO, ARHI, HLI, HLO, LO, LI, HO, HI, BO, BI, AI, SPOA, SPO, SPI, PCJ, PCO, PCI, HLT, controllogic_1_control_word[0]}));
  LED led_1 (.in(ARLO));
  LED led_2 (.in(ARHLO));
  LED led_3 (.in(ALUO));
  LED led_4 (.in(OPADD));
  LED led_5 (.in(OPSUB));
  LED led_6 (.in(OPNOT));
  LED led_7 (.in(OPNAND));
  LED led_8 (.in(OPSR));
  LED led_9 (.in(INCE));
  LED led_10 (.in(DEC));
  LED led_11 (.in(INCI));
  LED led_12 (.in(INCO));
  LED led_13 (.in(FI));
  LED led_14 (.in(FO));
  LED led_15 (.in(MI));
  LED led_16 (.in(MO));
  LED led_17 (.in(INI));
  LED led_18 (.in(RAMSTART));
  LED led_19 (.in(SPSTART));
  ALU alu_1 (
    .A_DATA_IN(aluregisters_1_a_data_out), .B_DATA_IN(aluregisters_1_b_data_out), .OP_NOT(OPNOT),
    .OP_NAND(OPNAND), .CARRY_IN(F_CARRY), .OP_ADD(OPADD), .OP_SUB(OPSUB), .OP_SR(OPSR), .RESULT_OUT(ALUO),
    .DATA_OUT(DATA_BUS), .CARRY_OUT(alu_1_carry_out[0]), .ZERO(alu_1_carry_out[1]),
    .SIGN(alu_1_carry_out[2]), .OVERFLOW(alu_1_carry_out[3]));
  LED led_20 (.in(HLT));
  LED led_21 (.in(PCI));
  LED led_22 (.in(PCO));
  LED led_23 (.in(PCJ));
  LED led_24 (.in(SPI));
  LED led_25 (.in(SPO));
  LED led_26 (.in(SPOA));
  LED led_27 (.in(AI));
  LED led_28 (.in(BI));
  LED led_29 (.in(BO));
  LED led_30 (.in(HI));
  LED led_31 (.in(HO));
  LED led_32 (.in(LI));
  LED led_33 (.in(LO));
  LED led_34 (.in(HLO));
  LED led_35 (.in(HLI));
  LED led_36 (.in(ARHI));
  LED led_37 (.in(ARHO));
  LED led_38 (.in(ARLI));
  Pull_Resistor pull_resistor_1 (.node(DATA_BUS));
  Pull_Resistor pull_resistor_2 (.node(ADDRESS_BUS));
  ALUFlags aluflags_1 (
    .CLK(CLK), .RESET(RESET), .DATA_IN(alu_1_carry_out), .ENABLE(FI),
    .DATA_OUT({aluflags_1_data_out, CONTROL_FLAGS[1:0]}));
  Incrementer incrementer_1 (
    .CLK(CLK), .RESET(RESET), .DATA_IN(DATA_BUS), .INCE(INCE), .DEC(DEC), .INCI(INCI), .INCO(INCO),
    .INCARRY_OUT(incrementer_1_incarry_out), .DATA_OUT(DATA_BUS));
  assign DATA_BUS[3:0] = FO ? {aluflags_1_data_out, CONTROL_FLAGS[1:0]} : 4'bz;  // Controlled_Buffer controlled_buffer_4
  Register #(.trigger("falling"), .width(1)) INCF (
    .D(incrementer_1_incarry_out), .en(INCE), .clk(CLK), .Q(CONTROL_FLAGS[2]), .clr(RESET));

  // Notes on the sheet:
  //   Tower
endmodule

module ProgramCounter (
  input  CLK,
  input  RESET,
  input  J,
  input  CO,
  input  CE,
  input  [15:0] PC_ADDRESS_IN,
  output [15:0] PC_DATA_OUT
);

  wire counter_1_carry;
  wire [15:0] counter_1_q;

  Counter #(.max('hffff), .width(16)) counter_1 (
    .clr(RESET), .load(J), .up(1'b1), .count(CE), .clk(CLK), .D(PC_ADDRESS_IN), .carry(counter_1_carry),
    .Q(counter_1_q));
  Pull_Resistor pull_resistor_1 (.node(counter_1_carry));
  assign PC_DATA_OUT = CO ? counter_1_q : 16'bz;  // Controlled_Buffer controlled_buffer_1

  // Notes on the sheet:
  //   Program Counter
endmodule

module ALU (
  input  [7:0] A_DATA_IN,
  input  [7:0] B_DATA_IN,
  input  OP_NOT,
  input  OP_NAND,
  input  CARRY_IN,
  input  OP_ADD,
  input  OP_SUB,
  input  OP_SR,
  input  RESULT_OUT,
  output [7:0] DATA_OUT,
  output CARRY_OUT,
  output ZERO,
  output SIGN,
  output OVERFLOW
);

  wire adder_1_cout, and_1_out, and_2_out, nor_1_out, or_1_out, or_2_out;
  wire [6:0] controlled_buffer_1_out;
  wire [7:0] adder_1_out, multiplexer_1_out, nand_1_out, not_1_out, not_2_out;

  // Probe on A_DATA_IN
  // Probe on B_DATA_IN
  or or_1 (or_1_out, OP_ADD, OP_SUB);
  assign not_1_out = ~A_DATA_IN;  // NOT_Gate not_1, 8 bits wide
  assign nand_1_out = ~(A_DATA_IN & B_DATA_IN);  // NAND_Gate nand_1, 8 bits wide
  or or_2 (or_2_out, CARRY_IN, OP_SUB);
  Multiplexer #(.width(8)) multiplexer_1 (.in0(B_DATA_IN), .in1(not_2_out), .out(multiplexer_1_out), .sel(OP_SUB));
  assign not_2_out = ~B_DATA_IN;  // NOT_Gate not_2, 8 bits wide
  nor nor_1 (nor_1_out, OP_NOT, OP_NAND, OP_ADD, OP_SUB, OP_SR);
  assign {SIGN, controlled_buffer_1_out} = nor_1_out ? A_DATA_IN : 8'bz;  // Controlled_Buffer controlled_buffer_1
  Adder adder_1 (.a(A_DATA_IN), .b(multiplexer_1_out), .out(adder_1_out), .cin(or_2_out), .cout(adder_1_cout));
  assign {SIGN, controlled_buffer_1_out} = OP_SR ? {1'b0, A_DATA_IN[7:1]} : 8'bz;  // Controlled_Buffer controlled_buffer_2
  assign {SIGN, controlled_buffer_1_out} = OP_NOT ? not_1_out : 8'bz;  // Controlled_Buffer controlled_buffer_3
  Pull_Resistor pull_resistor_1 (.node({SIGN, controlled_buffer_1_out}));
  assign {SIGN, controlled_buffer_1_out} = OP_NAND ? nand_1_out : 8'bz;  // Controlled_Buffer controlled_buffer_4
  assign {SIGN, controlled_buffer_1_out} = or_1_out ? adder_1_out : 8'bz;  // Controlled_Buffer controlled_buffer_5
  and and_1 (and_1_out, or_1_out, adder_1_cout);
  or or_3 (CARRY_OUT, and_1_out, and_2_out);
  and and_2 (and_2_out, A_DATA_IN[0], OP_SR);
  nor nor_2 (ZERO, SIGN, controlled_buffer_1_out[6], controlled_buffer_1_out[5], controlled_buffer_1_out[4], controlled_buffer_1_out[3], controlled_buffer_1_out[2], controlled_buffer_1_out[1], controlled_buffer_1_out[0]);
  assign DATA_OUT = RESULT_OUT ? {SIGN, controlled_buffer_1_out} : 8'bz;  // Controlled_Buffer controlled_buffer_6
  // Probe on DATA_OUT

  assign OVERFLOW = 1'b0;

  // Other names for the same wires on the sheet: OPADD = OP_ADD; OPNAND = OP_NAND; OPNOT = OP_NOT; OPSR = OP_SR;
  //   OPSUB = OP_SUB

  // Notes on the sheet:
  //   ALU
endmodule

module ALURegisters (
  input  CLK,
  input  RESET,
  input  [7:0] A_DATA_IN,
  input  AI,
  input  [7:0] B_DATA_IN,
  input  BI,
  output [7:0] A_DATA_OUT,
  output [7:0] B_DATA_OUT
);

  Register #(.trigger("falling")) A (.D(A_DATA_IN), .en(AI), .clk(CLK), .Q(A_DATA_OUT), .clr(RESET));
  Register #(.trigger("falling")) B (.D(B_DATA_IN), .en(BI), .clk(CLK), .Q(B_DATA_OUT), .clr(RESET));

  // Notes on the sheet:
  //   Registers
endmodule

module ALUFlags (
  input  CLK,
  input  RESET,
  input  [3:0] DATA_IN,
  input  ENABLE,
  output [3:0] DATA_OUT
);

  Register #(.width(4)) F (.D(DATA_IN), .en(ENABLE), .clk(CLK), .Q(DATA_OUT), .clr(RESET));

  // Notes on the sheet:
  //   Flags
endmodule

module Memory (
  input  CLK,
  input  [7:0] DATA_IN,
  input  [15:0] ADDR_IN,
  input  MI,
  input  MO,
  output [7:0] DATA_OUT
);

  wire and_1_out, or_1_out;
  wire [7:0] multiplexer_1_out, ram_1_dout, rom_1_data;

  ROM #(.addrWidth(16)) rom_1 (.addr(ADDR_IN), .data(rom_1_data));
  or or_1 (or_1_out, ADDR_IN[14], ADDR_IN[15]);
  and and_1 (and_1_out, or_1_out, MI);
  RAM #(.addrWidth(16)) ram_1 (.addr(ADDR_IN), .we(and_1_out), .oe(MO), .clk(CLK), .din(DATA_IN), .dout(ram_1_dout));
  Multiplexer #(.width(8)) multiplexer_1 (.in0(rom_1_data), .in1(ram_1_dout), .out(multiplexer_1_out), .sel(or_1_out));
  assign DATA_OUT = MO ? multiplexer_1_out : 8'bz;  // Controlled_Buffer controlled_buffer_1

  // Notes on the sheet:
  //   Memory
  //   contents of rom_1 (hex, n*v repeats v):
  //   9 ff 12 40 0 9 0 5a 0 15 21 1 12 40 1 14 40 0 52 0 7 e8
endmodule

module ControlLogic (
  input  CLK,
  input  RESET,
  input  [7:0] INSTRUCTION,
  input  [2:0] FLAGS,
  output [39:0] CONTROL_WORD
);

  wire or_1_out;
  wire [3:0] counter_1_q;

  or or_1 (or_1_out, RESET, CONTROL_WORD[0]);
  Counter #(.max('hf), .trigger("falling"), .width(4)) counter_1 (
    .clr(or_1_out), .load(1'b0), .up(1'b1), .clk(CLK), .Q(counter_1_q));  // open: count, D, carry
  ROM #(.addrWidth(15), .dataWidth(40)) rom_1 (.addr({INSTRUCTION, FLAGS, counter_1_q}), .data(CONTROL_WORD));

  // Other names for the same wires on the sheet: IEND = CONTROL_WORD[0]

  // Notes on the sheet:
  //   Control logic
  //   Step counter
  //   contents of rom_1 (hex, n*v repeats v):
  //   1800000008 4 1 1 12*0 1800000008 4 1 1 12*0 1800000008 4 1 1 12*0 1800000008 4 1 1 12*0 1800000008 4
  //   1 1 12*0 1800000008 4 1 1 12*0 1800000008 4 1 1 12*0 1800000008 4 1 1 1036*0 1800000008 4 800000108
  //   4 1 11*0 1800000008 4 800000108 4 1 11*0 1800000008 4 800000108 4 1 11*0 1800000008 4 800000108 4 1
  //   11*0 1800000008 4 800000108 4 1 11*0 1800000008 4 800000108 4 1 11*0 1800000008 4 800000108 4 1 11*0
  //   1800000008 4 800000108 4 1 139*0 1800000008 4 800020008 4 800080008 4 800200100 1 8*0 1800000008 4
  //   800020008 4 800080008 4 800200100 1 8*0 1800000008 4 800020008 4 800080008 4 800200100 1 8*0
  //   1800000008 4 800020008 4 800080008 4 800200100 1 8*0 1800000008 4 800020008 4 800080008 4 800200100
  //   1 8*0 1800000008 4 800020008 4 800080008 4 800200100 1 8*0 1800000008 4 800020008 4 800080008 4
  //   800200100 1 8*0 1800000008 4 800020008 4 800080008 4 800200100 1 8*0 1800000008 4 800020008 4
  //   800080008 4 800200800 40100000 90080000 40040000 90020000 800202000 800008100 1 0 0 1800000008 4
  //   800020008 4 800080008 4 800200800 40100000 90080000 40040000 90020000 800202000 800008100 1 0 0
  //   1800000008 4 800020008 4 800080008 4 800200800 40100000 90080000 40040000 90020000 800202000
  //   800008100 1 0 0 1800000008 4 800020008 4 800080008 4 800200800 40100000 90080000 40040000 90020000
  //   800202000 800008100 1 0 0 1800000008 4 800020008 4 800080008 4 800200800 40100000 90080000 40040000
  //   90020000 800202000 800008100 1 0 0 1800000008 4 800020008 4 800080008 4 800200800 40100000 90080000
  //   40040000 90020000 800202000 800008100 1 0 0 1800000008 4 800020008 4 800080008 4 200800 40100000
  //   90080000 40040000 90020000 800202000 800008100 1 0 0 1800000008 4 800020008 4 800080008 4 800200800
  //   40100000 90080000 40040000 90020000 800202000 800008100 1 0 0 1800000008 4 800080008 4 2800200100 1
  //   10*0 1800000008 4 800080008 4 2800200100 1 10*0 1800000008 4 800080008 4 2800200100 1 10*0
  //   1800000008 4 800080008 4 2800200100 1 10*0 1800000008 4 800080008 4 2800200100 1 10*0 1800000008 4
  //   800080008 4 2800200100 1 10*0 1800000008 4 800080008 4 2800200100 1 10*0 1800000008 4 800080008 4
  //   2800200100 1 522*0 1800000008 4 800020008 4 800080008 4 400600000 1 8*0 1800000008 4 800020008 4
  //   800080008 4 400600000 1 8*0 1800000008 4 800020008 4 800080008 4 400600000 1 8*0 1800000008 4
  //   800020008 4 800080008 4 400600000 1 8*0 1800000008 4 800020008 4 800080008 4 400600000 1 8*0
  //   1800000008 4 800020008 4 800080008 4 400600000 1 8*0 1800000008 4 800020008 4 800080008 4 400600000
  //   1 8*0 1800000008 4 800020008 4 800080008 4 400600000 1 136*0 1800000008 4 800020008 4 800080008 4
  //   800200800 40100000 90080000 800202000 400408000 1 4*0 1800000008 4 800020008 4 800080008 4 800200800
  //   40100000 90080000 800202000 400408000 1 4*0 1800000008 4 800020008 4 800080008 4 800200800 40100000
  //   90080000 800202000 400408000 1 4*0 1800000008 4 800020008 4 800080008 4 800200800 40100000 90080000
  //   800202000 400408000 1 4*0 1800000008 4 800020008 4 800080008 4 800200800 40100000 90080000 40040000
  //   90020000 800202000 400408000 1 0 0 1800000008 4 800020008 4 800080008 4 800200800 40100000 90080000
  //   40040000 90020000 800202000 400408000 1 0 0 1800000008 4 800020008 4 800080008 4 800200800 40100000
  //   90080000 40040000 90020000 800202000 400408000 1 0 0 1800000008 4 800020008 4 800080008 4 800200800
  //   40100000 90080000 40040000 90020000 800202000 400408000 1 0 0 1800000008 4 800080008 4 2400600000 1
  //   10*0 1800000008 4 800080008 4 2400600000 1 10*0 1800000008 4 800080008 4 2400600000 1 10*0
  //   1800000008 4 800080008 4 2400600000 1 10*0 1800000008 4 800080008 4 2400600000 1 10*0 1800000008 4
  //   800080008 4 2400600000 1 10*0 1800000008 4 800080008 4 2400600000 1 10*0 1800000008 4 800080008 4
  //   2400600000 1 1418*0 1800000008 4 800000208 4 100c00100 1 10*0 1800000008 4 800000208 4 100c00100 1
  //   10*0 1800000008 4 800000208 4 100c00100 1 10*0 1800000008 4 800000208 4 100c00100 1 10*0 1800000008
  //   4 800000208 4 100c00100 1 10*0 1800000008 4 800000208 4 100c00100 1 10*0 1800000008 4 800000208 4
  //   100c00100 1 10*0 1800000008 4 800000208 4 100c00100 1 138*0 1800000008 4 80002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
  //   Microcode
endmodule

module InstructionRegister (
  input  CLK,
  input  RESET,
  input  [7:0] DATA_IN,
  input  INI,
  output [7:0] DATA_OUT
);

  Register #(.trigger("falling")) register_1 (.D(DATA_IN), .en(INI), .clk(CLK), .Q(DATA_OUT), .clr(RESET));

  // Notes on the sheet:
  //   Instruction register
endmodule

module ArgumentRegisters (
  input  CLK,
  input  RESET,
  input  [7:0] DATA_IN,
  input  HI,
  input  LI,
  input  HO,
  input  LO,
  input  HLO,
  output [7:0] DATA_OUT,
  output [15:0] ADDRESS_OUT
);

  wire [7:0] ARH_q, ARL_q;

  Register #(.trigger("falling")) ARH (.D(DATA_IN), .en(HI), .clk(CLK), .Q(ARH_q), .clr(RESET));
  Register #(.trigger("falling")) ARL (.D(DATA_IN), .en(LI), .clk(CLK), .Q(ARL_q), .clr(RESET));
  assign DATA_OUT = HO ? ARH_q : 8'bz;  // Controlled_Buffer controlled_buffer_1
  assign DATA_OUT = LO ? ARL_q : 8'bz;  // Controlled_Buffer controlled_buffer_2
  assign ADDRESS_OUT = HLO ? {ARH_q, ARL_q} : 16'bz;  // Controlled_Buffer controlled_buffer_3

  // Other names for the same wires on the sheet: ARHI = HI; ARHLO = HLO; ARHO = HO; ARLI = LI; ARLO = LO

  // Notes on the sheet:
  //   Argument registers
endmodule

module MemoryRegisters (
  input  CLK,
  input  RESET,
  input  [15:0] ADDRESS_IN,
  input  [7:0] DATA_IN,
  input  HI,
  input  LI,
  input  HO,
  input  LO,
  input  HLO,
  input  HLI,
  output [7:0] DATA_OUT,
  output [15:0] ADDRESS_OUT
);

  wire [7:0] H_q, L_q, multiplexer_1_out, multiplexer_2_out;

  Register #(.trigger("falling")) H (.D(multiplexer_1_out), .en(HI), .clk(CLK), .Q(H_q), .clr(RESET));
  Multiplexer #(.width(8)) multiplexer_1 (.in0(DATA_IN), .in1(ADDRESS_IN[15:8]), .out(multiplexer_1_out), .sel(HLI));
  Register #(.trigger("falling")) L (.D(multiplexer_2_out), .en(LI), .clk(CLK), .Q(L_q), .clr(RESET));
  Multiplexer #(.width(8)) multiplexer_2 (.in0(DATA_IN), .in1(ADDRESS_IN[7:0]), .out(multiplexer_2_out), .sel(HLI));
  assign DATA_OUT = HO ? H_q : 8'bz;  // Controlled_Buffer controlled_buffer_1
  assign DATA_OUT = LO ? L_q : 8'bz;  // Controlled_Buffer controlled_buffer_2
  assign ADDRESS_OUT = HLO ? {H_q, L_q} : 16'bz;  // Controlled_Buffer controlled_buffer_3

  // Notes on the sheet:
  //   Memory registers
endmodule

module StackPointer (
  input  CLK,
  input  RESET,
  input  [7:0] DATA_IN,
  input  SPI,
  input  SPO,
  output [7:0] DATA_OUT
);

  wire [7:0] register_1_q;

  Register #(.trigger("falling")) register_1 (.D(DATA_IN), .en(SPI), .clk(CLK), .Q(register_1_q), .clr(RESET));
  assign DATA_OUT = SPO ? register_1_q : 8'bz;  // Controlled_Buffer controlled_buffer_1

  // Notes on the sheet:
  //   Stack pointer
endmodule

module Incrementer (
  input  CLK,
  input  RESET,
  input  [7:0] DATA_IN,
  input  INCE,
  input  DEC,
  input  INCI,
  input  INCO,
  output INCARRY_OUT,
  output [7:0] DATA_OUT
);

  wire and_1_out, counter_1_carry, not_1_out;
  wire [7:0] counter_1_q;

  Counter counter_1 (
    .clr(RESET), .load(INCI), .up(not_1_out), .count(INCE), .clk(CLK), .D(DATA_IN), .carry(counter_1_carry),
    .Q(counter_1_q));
  not not_1 (not_1_out, DEC);
  assign DATA_OUT = INCO ? counter_1_q : 8'bz;  // Controlled_Buffer controlled_buffer_1
  D_Flip_Flop d_ff_1 (.D(counter_1_carry), .clk(and_1_out), .Q(INCARRY_OUT));  // open: Qn, preset, reset
  and and_1 (and_1_out, CLK, INCE);

  // Notes on the sheet:
  //   Incrementer
endmodule
